// Logisim project 1 - Somador 16 bits.circ as structural Verilog: 1 circuit, main circuit main
module main (
  input  [15:0] B,
  input  [15:0] B_2,
  output [16:0] C
);

  wire clock_1_out, main_1_c, main_1_vaium, main_2_c, main_2_vaium, main_3_c, main_3_vaium, main_4_c,
       main_4_vaium, main_5_c, main_5_vaium, main_6_c, main_6_vaium, main_7_c, main_7_vaium, main_8_c,
       main_8_vaium, main_9_c, main_9_vaium, main_10_c, main_10_vaium, main_11_c, main_11_vaium, main_12_c,
       main_12_vaium, main_13_c, main_13_vaium, main_14_c, main_14_vaium, main_15_c, main_15_vaium,
       main_16_c, main_16_vaium;

  Clock clock_1 (.out(clock_1_out));
  Somador_1_bit_main main_1 (.VaiUm(main_1_vaium), .B(B_2[14]), .A(B[14]), .C(main_1_c), .VemUm(main_3_vaium));
  Somador_1_bit_main main_2 (.VaiUm(main_2_vaium), .B(B_2[15]), .A(B[15]), .C(main_2_c), .VemUm(main_1_vaium));
  D_Flip_Flop d_ff_1 (.clk(clock_1_out), .D(main_1_c), .Q(C[14]), .en(1'b1));  // open: Qn, preset, reset
  D_Flip_Flop d_ff_2 (.clk(clock_1_out), .D(main_2_c), .Q(C[15]), .en(1'b1));  // open: Qn, preset, reset
  D_Flip_Flop d_ff_3 (.clk(clock_1_out), .D(main_2_vaium), .Q(C[16]), .en(1'b1));  // open: Qn, preset, reset
  Somador_1_bit_main main_3 (.VaiUm(main_3_vaium), .B(B_2[13]), .A(B[13]), .C(main_3_c), .VemUm(main_5_vaium));
  D_Flip_Flop d_ff_4 (.clk(clock_1_out), .D(main_6_c), .Q(C[10]), .en(1'b1));  // open: Qn, preset, reset
  D_Flip_Flop d_ff_5 (.clk(clock_1_out), .D(main_4_c), .Q(C[11]), .en(1'b1));  // open: Qn, preset, reset
  D_Flip_Flop d_ff_6 (.clk(clock_1_out), .D(main_5_c), .Q(C[12]), .en(1'b1));  // open: Qn, preset, reset
  D_Flip_Flop d_ff_7 (.clk(clock_1_out), .D(main_3_c), .Q(C[13]), .en(1'b1));  // open: Qn, preset, reset
  Somador_1_bit_main main_4 (.VaiUm(main_4_vaium), .B(B_2[11]), .A(B[11]), .C(main_4_c), .VemUm(main_6_vaium));
  Somador_1_bit_main main_5 (.VaiUm(main_5_vaium), .B(B_2[12]), .A(B[12]), .C(main_5_c), .VemUm(main_4_vaium));
  Somador_1_bit_main main_6 (.VaiUm(main_6_vaium), .B(B_2[10]), .A(B[10]), .C(main_6_c), .VemUm(main_7_vaium));
  Somador_1_bit_main main_7 (.VaiUm(main_7_vaium), .B(B_2[9]), .A(B[9]), .C(main_7_c), .VemUm(main_8_vaium));
  Somador_1_bit_main main_8 (.VaiUm(main_8_vaium), .B(B_2[8]), .A(B[8]), .C(main_8_c), .VemUm(main_10_vaium));
  D_Flip_Flop d_ff_8 (.clk(clock_1_out), .D(main_8_c), .Q(C[8]), .en(1'b1));  // open: Qn, preset, reset
  D_Flip_Flop d_ff_9 (.clk(clock_1_out), .D(main_7_c), .Q(C[9]), .en(1'b1));  // open: Qn, preset, reset
  Somador_1_bit_main main_9 (.VaiUm(main_9_vaium), .B(B_2[6]), .A(B[6]), .C(main_9_c), .VemUm(main_11_vaium));
  Somador_1_bit_main main_10 (.VaiUm(main_10_vaium), .B(B_2[7]), .A(B[7]), .C(main_10_c), .VemUm(main_9_vaium));
  D_Flip_Flop d_ff_10 (.clk(clock_1_out), .D(main_9_c), .Q(C[6]), .en(1'b1));  // open: Qn, preset, reset
  D_Flip_Flop d_ff_11 (.clk(clock_1_out), .D(main_10_c), .Q(C[7]), .en(1'b1));  // open: Qn, preset, reset
  Somador_1_bit_main main_11 (.VaiUm(main_11_vaium), .B(B_2[5]), .A(B[5]), .C(main_11_c), .VemUm(main_13_vaium));
  D_Flip_Flop d_ff_12 (.clk(clock_1_out), .D(main_11_c), .Q(C[5]), .en(1'b1));  // open: Qn, preset, reset
  Somador_1_bit_main main_12 (.VaiUm(main_12_vaium), .B(B_2[3]), .A(B[3]), .C(main_12_c), .VemUm(main_14_vaium));
  Somador_1_bit_main main_13 (.VaiUm(main_13_vaium), .B(B_2[4]), .A(B[4]), .C(main_13_c), .VemUm(main_12_vaium));
  D_Flip_Flop d_ff_13 (.clk(clock_1_out), .D(main_13_c), .Q(C[4]));  // open: Qn, preset, en, reset
  D_Flip_Flop d_ff_14 (.clk(clock_1_out), .D(main_12_c), .Q(C[3]), .en(1'b1));  // open: Qn, preset, reset
  Somador_1_bit_main main_14 (.VaiUm(main_14_vaium), .B(B_2[2]), .A(B[2]), .C(main_14_c), .VemUm(main_15_vaium));
  D_Flip_Flop d_ff_15 (.clk(clock_1_out), .D(main_14_c), .Q(C[2]), .en(1'b1));  // open: Qn, preset, reset
  Somador_1_bit_main main_15 (.VaiUm(main_15_vaium), .B(B_2[1]), .A(B[1]), .C(main_15_c), .VemUm(main_16_vaium));
  Somador_1_bit_main main_16 (.VaiUm(main_16_vaium), .B(B_2[0]), .A(B[0]), .C(main_16_c), .VemUm(1'b0));
  D_Flip_Flop d_ff_16 (.clk(clock_1_out), .D(main_15_c), .Q(C[1]), .en(1'b1));  // open: Qn, preset, reset
  D_Flip_Flop d_ff_17 (.clk(clock_1_out), .D(main_16_c), .Q(C[0]), .en(1'b1));  // open: Qn, preset, reset
endmodule
