// Logisim project Contador com FLIP-FLOP T crescente 3bits Entrada.circ as structural Verilog: 1 circuit, main circuit main
module main (
  input  E,
  output [2:0] S
);

  wire t_ff_2_qn, t_ff_3_qn;

  T_Flip_Flop t_ff_1 (.clk(t_ff_2_qn), .T(1'b1), .Q(S[2]));  // open: Qn, preset, reset, en
  T_Flip_Flop t_ff_2 (.clk(t_ff_3_qn), .T(1'b1), .Q(S[1]), .Qn(t_ff_2_qn));  // open: preset, reset, en
  T_Flip_Flop t_ff_3 (.clk(E), .T(1'b1), .Q(S[0]), .Qn(t_ff_3_qn));  // open: preset, reset, en
endmodule
