// Logisim project Contador com FLIP-FLOP T crescente.circ as structural Verilog: 1 circuit, main circuit main
module main (
  output [3:0] out_1
);

  wire clock_1_out, t_ff_2_qn, t_ff_3_qn, t_ff_4_qn;

  T_Flip_Flop t_ff_1 (.clk(t_ff_2_qn), .T(1'b1), .Q(out_1[3]));  // open: Qn, preset, reset, en
  T_Flip_Flop t_ff_2 (.clk(t_ff_3_qn), .T(1'b1), .Q(out_1[2]), .Qn(t_ff_2_qn));  // open: preset, reset, en
  T_Flip_Flop t_ff_3 (.clk(t_ff_4_qn), .T(1'b1), .Q(out_1[1]), .Qn(t_ff_3_qn));  // open: preset, reset, en
  T_Flip_Flop t_ff_4 (.clk(clock_1_out), .T(1'b1), .Q(out_1[0]), .Qn(t_ff_4_qn));  // open: preset, reset, en
  Clock clock_1 (.out(clock_1_out));
endmodule
