// Logisim project Contador com Master-Slave crescente.circ as structural Verilog: 1 circuit, main circuit main
module main (
  input  in_1,
  output [3:0] out_2,
  output out_3,
  output out_4,
  output out_5,
  output out_6
);

  // FLIO_FLOP_Master_Slave_main main_1: pin names not known; wires that end beside it: 1'b1, in_1, 1'b1, out_2[0]
  // FLIO_FLOP_Master_Slave_main main_2: pin names not known; wires that end beside it: 1'b1, out_2[0], 1'b1, out_2[1]
  // FLIO_FLOP_Master_Slave_main main_3: pin names not known; wires that end beside it: 1'b1, out_2[1], 1'b1, out_2[2]
  // FLIO_FLOP_Master_Slave_main main_4: pin names not known; wires that end beside it: 1'b1, out_2[2], 1'b1, out_2[3]

  assign out_3 = out_2[0];
  assign out_4 = out_2[1];
  assign out_5 = out_2[2];
  assign out_6 = out_2[3];
endmodule
