// Logisim project FLIP-FLOP Master-Slave.circ as structural Verilog: 1 circuit, main circuit main
module main (
  input  in_1,
  input  in_2,
  input  in_3,
  output out_4,
  output out_5
);

  wire and_1_out, and_2_out, and_3_out, and_4_out, not_1_out, s_r_ff_1_q, s_r_ff_1_qn;

  and and_1 (and_1_out, s_r_ff_1_qn, out_5, in_1);
  and and_2 (and_2_out, in_3, out_4, s_r_ff_1_q);
  S_R_Flip_Flop s_r_ff_1 (
    .S(and_1_out), .clk(in_2), .R(and_2_out), .Q(s_r_ff_1_q), .Qn(s_r_ff_1_qn));  // open: preset, reset, en
  and and_3 (and_3_out, out_5, s_r_ff_1_q);
  and and_4 (and_4_out, s_r_ff_1_qn, out_4);
  S_R_Flip_Flop s_r_ff_2 (
    .S(and_3_out), .clk(not_1_out), .R(and_4_out), .Q(out_4), .Qn(out_5));  // open: preset, reset, en
  not not_1 (not_1_out, in_2);
endmodule
