// Logisim project Multiplicador.circ as structural Verilog: 1 circuit, main circuit main
module main (
  input  [7:0] zero,
  input  [7:0] Multiplicando,
  input  in_3,
  input  [7:0] Multiplicador,
  output [7:0] out_5
);

  wire clock_1_out;
  wire [2:0] main_1_s;
  wire [7:0] adder_1_out, multiplexer_1_out, shifter_1_out, shifter_2_out;

  Contador_com_FLIP_FLOP_T_crescente_3bits_Entrada_main main_1 (.S(main_1_s), .E(clock_1_out));
  Shifter shifter_1 (.in(Multiplicando), .\dist (main_1_s), .out(shifter_1_out));
  Clock clock_1 (.out(clock_1_out));
  Multiplexer #(.width(8)) multiplexer_1 (
    .in0(zero), .in1(shifter_1_out), .out(multiplexer_1_out), .sel(shifter_2_out[0]));  // open: en
  Shifter #(.shift("lr")) shifter_2 (.in(Multiplicador), .\dist (main_1_s), .out(shifter_2_out));
  Adder adder_1 (.a(multiplexer_1_out), .b(out_5), .out(adder_1_out));  // open: cin, cout
  Register register_1 (.D(adder_1_out), .en(1'b1), .Q(out_5), .clk(clock_1_out), .clr(in_3));
endmodule
