// Logisim project Máquina de Estado com FLIP-FLOP T.circ as structural Verilog: 1 circuit, main circuit main
module main (
  output [3:0] out_1
);

  wire clock_1_out, t_ff_1_qn, t_ff_2_q;

  Clock clock_1 (.out(clock_1_out));
  T_Flip_Flop t_ff_1 (.clk(clock_1_out), .T(1'b1), .Q(out_1[0]), .Qn(t_ff_1_qn));  // open: preset, reset, en
  xor xor_1 (out_1[1], out_1[0], t_ff_2_q);
  T_Flip_Flop t_ff_2 (.clk(t_ff_1_qn), .T(1'b1), .Q(t_ff_2_q));  // open: Qn, preset, reset, en
  xor xor_2 (out_1[2], out_1[3], t_ff_2_q);
  and and_1 (out_1[3], out_1[0], t_ff_2_q);
endmodule
