// Logisim project Máquina de Estado com Master-Slave.circ as structural Verilog: 1 circuit, main circuit main
module main (
  output [3:0] out_1
);

  wire clock_1_out, main_1_out_4, main_2_out_5, main_3_out_4, main_4_out_4;

  Clock clock_1 (.out(clock_1_out));
  FLIP_FLOP_Master_Slave_main main_1 (
    .in_1(1'b1), .in_2(clock_1_out), .in_3(1'b1), .out_4(main_1_out_4));  // open: out_5
  FLIP_FLOP_Master_Slave_main main_2 (
    .in_1(1'b1), .in_2(clock_1_out), .in_3(1'b1), .out_4(out_1[0]), .out_5(main_2_out_5));
  FLIP_FLOP_Master_Slave_main main_3 (
    .in_1(1'b1), .in_2(main_2_out_5), .in_3(1'b1), .out_4(main_3_out_4));  // open: out_5
  xor xor_1 (out_1[2], main_4_out_4, out_1[3]);
  xor xor_2 (out_1[1], out_1[0], main_4_out_4);
  FLIP_FLOP_Master_Slave_main main_4 (
    .in_1(1'b1), .in_2(main_1_out_4), .in_3(1'b1), .out_4(main_4_out_4));  // open: out_5
  and and_1 (out_1[3], main_4_out_4, main_3_out_4);
endmodule
