// Logisim project 1 - Somador 8 bits.circ as structural Verilog: 1 circuit, main circuit main
module main (
  input  [7:0] A,
  input  [7:0] B,
  output [8:0] C
);

  wire main_1_vaium, main_3_vaium, main_4_vaium, main_5_vaium, main_6_vaium, main_7_vaium, main_8_vaium;

  Somador_1_bit_main main_1 (.VaiUm(main_1_vaium), .B(B[6]), .A(A[6]), .C(C[6]), .VemUm(main_3_vaium));
  Somador_1_bit_main main_2 (.VaiUm(C[8]), .B(B[7]), .A(A[7]), .C(C[7]), .VemUm(main_1_vaium));
  Somador_1_bit_main main_3 (.VaiUm(main_3_vaium), .B(B[5]), .A(A[5]), .C(C[5]), .VemUm(main_4_vaium));
  Somador_1_bit_main main_4 (.VaiUm(main_4_vaium), .B(B[4]), .A(A[4]), .C(C[4]), .VemUm(main_5_vaium));
  Somador_1_bit_main main_5 (.VaiUm(main_5_vaium), .B(B[3]), .A(A[3]), .C(C[3]), .VemUm(main_6_vaium));
  Somador_1_bit_main main_6 (.VaiUm(main_6_vaium), .B(B[2]), .A(A[2]), .C(C[2]), .VemUm(main_7_vaium));
  Somador_1_bit_main main_7 (.VaiUm(main_7_vaium), .B(B[1]), .A(A[1]), .C(C[1]), .VemUm(main_8_vaium));
  Somador_1_bit_main main_8 (.VaiUm(main_8_vaium), .B(B[0]), .A(A[0]), .C(C[0]), .VemUm(1'b0));
endmodule
