// Logisim project 2 - Decodificador 4 bits.circ as structural Verilog: 1 circuit, main circuit main
module main (
  input  in_1,
  input  in_2,
  input  in_3,
  input  in_4,
  input  in_5
);

  wire main_1_saidab, main_2_saidac, main_3_out_5, main_4_saidae, main_5_saidag, main_6_out_5, main_7_saidaa,
       undriven;

  B_main main_1 (.a3(in_1), .a2(in_2), .a1(in_3), .a0(in_4), .SaidaB(main_1_saidab));
  C_main main_2 (.a3(in_1), .a2(in_2), .a1(in_3), .a0(in_4), .SaidaC(main_2_saidac));
  D_main main_3 (.a3(in_1), .a2(in_2), .a1(in_3), .a0(in_4), .out_5(main_3_out_5));
  E_main main_4 (.a3(in_1), .a2(in_2), .a1(in_3), .a0(in_4), .SaidaE(main_4_saidae));
  G_main main_5 (.a3(in_1), .a2(in_2), .a1(in_3), .a0(in_4), .SaidaG(main_5_saidag));
  H_main main_6 (.a3(in_1), .a2(in_2), .a1(in_3), .a0(in_4), .out_5(main_6_out_5));
  A_main main_7 (.saidaA(main_7_saidaa), .a3(in_1), .a2(in_2), .a1(in_3), .a0(in_4));
  _7_Segment_Display u_7_segment_display_1 (
    .g(main_2_saidac), .f(main_7_saidaa), .a(main_1_saidab), .b(main_3_out_5), .e(main_4_saidae),
    .d(main_5_saidag), .c(main_6_out_5), .dp(undriven));

  // Notes on the sheet:
  //   A
  //   B
  //   C
  //   D
  //   E
  //   G
  //   H
endmodule
