// Logisim project 3 - ULA.circ as structural Verilog: 1 circuit, main circuit main
module main (
  input  [7:0] A,
  input  [7:0] B,
  input  [1:0] OP,
  output [7:0] S
);

  wire [7:0] Bitwise_AND_c, Bitwise_OR_c;
  wire [8:0] Somador_p1, Subtrator_s;

  // Somador_8_bits_main Somador: pin names not known; wires that end beside it: Somador_p1, A, B
  Subtrator_8_bits_main Subtrator (.S(Subtrator_s), .B(B), .A(A));
  BitwiseAND_main Bitwise_AND (.C(Bitwise_AND_c), .A(A), .B(B));
  BitwiseOr_main Bitwise_OR (.C(Bitwise_OR_c), .A(A), .B(B));
  Multiplexer #(.select(2), .width(8), .enable("false")) multiplexer_1 (
    .in0(Somador_p1[7:0]), .in1(Subtrator_s[7:0]), .in2(Bitwise_AND_c), .in3(Bitwise_OR_c), .out(S), .sel(OP));
endmodule
