// Logisim project BitwiseAND.circ as structural Verilog: 1 circuit, main circuit main
module main (
  input  [7:0] A,
  input  [7:0] B,
  output [7:0] C
);

  and and_1 (C[7], B[7], A[7]);
  and and_2 (C[6], B[6], A[6]);
  and and_3 (C[5], B[5], A[5]);
  and and_4 (C[4], B[4], A[4]);
  and and_5 (C[3], B[3], A[3]);
  and and_6 (C[1], B[1], A[1]);
  and and_7 (C[2], B[2], A[2]);
  and and_8 (C[0], B[0], A[0]);
endmodule
