// Logisim project D.circ as structural Verilog: 1 circuit, main circuit main
module main (
  input  a3,
  input  a2,
  input  a1,
  input  a0,
  output out_5
);

  wire and_1_out, and_2_out, and_3_out, and_4_out, and_5_out, not_1_out, not_2_out, not_3_out, not_4_out,
       not_5_out, not_6_out, not_7_out, not_8_out, not_9_out;

  not not_1 (not_1_out, a2);
  and and_1 (and_1_out, not_1_out, not_2_out);
  not not_2 (not_2_out, a1);
  not not_3 (not_3_out, a2);
  and and_2 (and_2_out, not_3_out, not_4_out);
  not not_4 (not_4_out, a0);
  not not_5 (not_5_out, a3);
  and and_3 (and_3_out, not_5_out, not_6_out, not_7_out);
  not not_6 (not_6_out, a1);
  not not_7 (not_7_out, a0);
  not not_8 (not_8_out, a3);
  and and_4 (and_4_out, not_8_out, a1, a0);
  not not_9 (not_9_out, a1);
  and and_5 (and_5_out, a3, not_9_out, a0);
  or or_1 (out_5, and_1_out, and_2_out, and_3_out, and_4_out, and_5_out);
endmodule
