// Logisim project E.circ as structural Verilog: 1 circuit, main circuit main
module main (
  input  a3,
  input  a2,
  input  a1,
  input  a0,
  output SaidaE
);

  wire and_1_out, and_2_out, and_3_out, and_4_out, and_5_out, not_1_out, not_2_out, not_3_out, not_4_out;

  and and_1 (and_1_out, a3, a2);
  and and_2 (and_2_out, a1, not_1_out);
  not not_1 (not_1_out, a0);
  and and_3 (and_3_out, a3, a1);
  and and_4 (and_4_out, a3, not_2_out);
  not not_2 (not_2_out, a0);
  not not_3 (not_3_out, a2);
  and and_5 (and_5_out, not_3_out, not_4_out);
  not not_4 (not_4_out, a0);
  or or_1 (SaidaE, and_1_out, and_2_out, and_3_out, and_4_out, and_5_out);
endmodule
