// Logisim project Somador 1 bit.circ as structural Verilog: 1 circuit, main circuit main
module main (
  input  B,
  input  A,
  input  VemUm,
  output VaiUm,
  output C
);

  wire and_1_out, and_2_out, xor_1_out;

  or or_1 (VaiUm, and_1_out, and_2_out);
  and and_1 (and_1_out, B, A);
  xor xor_1 (xor_1_out, B, A);
  and and_2 (and_2_out, xor_1_out, VemUm);
  xor xor_2 (C, xor_1_out, VemUm);
endmodule
