// Logisim project Subtrator 8 bits.circ as structural Verilog: 1 circuit, main circuit main
module main (
  input  [7:0] B,
  input  [7:0] A,
  output [8:0] S
);

  wire main_2_vaium, main_4_vaium, main_5_vaium, main_6_vaium, main_7_vaium, main_8_vaium, main_9_vaium,
       main_10_vaium, main_11_vaium, main_12_vaium, main_13_vaium, main_14_vaium, main_15_vaium,
       main_16_vaium;
  wire [7:0] not_1_out;
  wire [8:0] main_3_vaium;

  Somador_1_bit_main main_1 (.VaiUm(S[8]), .B(A[7]), .A(main_3_vaium[7]), .C(S[7]), .VemUm(main_4_vaium));
  Somador_1_bit_main main_2 (
    .VaiUm(main_2_vaium), .B(not_1_out[6]), .A(1'b0), .C(main_3_vaium[6]), .VemUm(main_5_vaium));
  Somador_1_bit_main main_3 (
    .VaiUm(main_3_vaium[8]), .B(not_1_out[7]), .A(1'b0), .C(main_3_vaium[7]), .VemUm(main_2_vaium));
  Somador_1_bit_main main_4 (.VaiUm(main_4_vaium), .B(A[6]), .A(main_3_vaium[6]), .C(S[6]), .VemUm(main_7_vaium));
  Somador_1_bit_main main_5 (
    .VaiUm(main_5_vaium), .B(not_1_out[5]), .A(1'b0), .C(main_3_vaium[5]), .VemUm(main_9_vaium));
  Somador_1_bit_main main_6 (.VaiUm(main_6_vaium), .B(A[4]), .A(main_3_vaium[4]), .C(S[4]), .VemUm(main_10_vaium));
  Somador_1_bit_main main_7 (.VaiUm(main_7_vaium), .B(A[5]), .A(main_3_vaium[5]), .C(S[5]), .VemUm(main_6_vaium));
  Somador_1_bit_main main_8 (
    .VaiUm(main_8_vaium), .B(not_1_out[3]), .A(1'b0), .C(main_3_vaium[3]), .VemUm(main_11_vaium));
  Somador_1_bit_main main_9 (
    .VaiUm(main_9_vaium), .B(not_1_out[4]), .A(1'b0), .C(main_3_vaium[4]), .VemUm(main_8_vaium));
  Somador_1_bit_main main_10 (.VaiUm(main_10_vaium), .B(A[3]), .A(main_3_vaium[3]), .C(S[3]), .VemUm(main_13_vaium));
  Somador_1_bit_main main_11 (
    .VaiUm(main_11_vaium), .B(not_1_out[2]), .A(1'b0), .C(main_3_vaium[2]), .VemUm(main_12_vaium));
  Somador_1_bit_main main_12 (
    .VaiUm(main_12_vaium), .B(not_1_out[1]), .A(1'b0), .C(main_3_vaium[1]), .VemUm(main_15_vaium));
  Somador_1_bit_main main_13 (.VaiUm(main_13_vaium), .B(A[2]), .A(main_3_vaium[2]), .C(S[2]), .VemUm(main_14_vaium));
  Somador_1_bit_main main_14 (.VaiUm(main_14_vaium), .B(A[1]), .A(main_3_vaium[1]), .C(S[1]), .VemUm(main_16_vaium));
  Somador_1_bit_main main_15 (.VaiUm(main_15_vaium), .B(not_1_out[0]), .A(1'b1), .C(main_3_vaium[0]), .VemUm(1'b0));
  Somador_1_bit_main main_16 (.VaiUm(main_16_vaium), .B(A[0]), .A(main_3_vaium[0]), .C(S[0]), .VemUm(1'b0));
  assign not_1_out = ~B;  // NOT_Gate not_1, 8 bits wide
endmodule
